# Fritzing sketch rfid_door (saved by Fritzing 0.8.7b)
breadboards: 1

parts:
  Raspberry_Pi_B_rev1 = Raspberry Pi B rev2
  J1 = female pin header, 2 pins [form="♀ (female)"]
  J2 = female pin header, 2 pins [form="♀ (female)"]
  Composant1 = Logic Level Converter
  J3 = female pin header, 2 pins [form="♀ (female)"]
  R1 = Resistor [tolerance=±5% resistance=370 package=THT]
  J4 = female pin header, 3 pins [form="♀ (female)"]

nets:
  N1: Raspberry_Pi_B_rev1.3V3, Composant1.LV
  N2: Raspberry_Pi_B_rev1.5V, J2.pin1, Composant1.HV, J4.pin2
  GND: Raspberry_Pi_B_rev1.GND, J2.pin2, Composant1.GND, J3.pin2, J4.pin3
  N3: Raspberry_Pi_B_rev1.GPIO_14, Composant1.TX_LV
  N4: Raspberry_Pi_B_rev1.GPIO_15, Composant1.RX_LV
  N5: Raspberry_Pi_B_rev1.GPIO_17, J4.pin1
  N6: Raspberry_Pi_B_rev1.GPIO_4, R1.Pin_0
  N7: J1.pin1, Composant1.TX_HV
  N8: J1.pin2, Composant1.RX_HV
  N9: J3.pin1, R1.Pin_1

notes:
  5V
  3.3V
  Connecteur lecteur RFID MFRC522
  RX / TX / VCC / GND
  Connecteur led
  anode / cathode
  Connecteur relai
  commande, VCC, GND
